# Fritzing sketch GEH KS 28 Uno PCB (saved by Fritzing 0.9.6b)
circuit board: 6.70001cm x 4.51063cm
breadboards: 1

parts:
  U1 = atmega328 [package=dip]
  S1 = Pushbutton [package="[THT]"]
  R1 = Resistor [tolerance=±5% power=0.25 resistance=220 package=THT]
  U2 = Voltage Regulator - 3.3V [package="TO220 [THT]"]
  C1 = Electrolytic Capacitor [capacitance=1µF voltage=35V package="100 mil [THT, electrolytic]"]
  J1 = Screw terminal - 2 pins [package=THT]
  C2 = Electrolytic Capacitor [capacitance=1µF voltage=35V package="100 mil [THT, electrolytic]"]
  C3 = Capacitor [package=cap-pth-small2]
  C4 = Capacitor [package=cap-pth-small2]
  XTAL1 = Crystal [frequency="16 Mhz" package=THT]
  LED1 = LED - 5mm [color="Red (633nm)" current=0.030 package="5 mm [THT]"]
  R2 = Resistor [tolerance=±5% power=0.25 resistance=220 package=THT]
  C5 = Ceramic Capacitor [capacitance=10nF voltage=35V package="100 mil [THT, multilayer]"]
  J12 = female pin header, 5 pins [form="♀ (female)"]
  J26 = female pin header, 20 pins [form="♀ (female)"]
  J27 = female pin header, 20 pins [form="♀ (female)"]
  J28 = female pin header, 20 pins [form="♀ (female)"]
  J29 = female pin header, 20 pins [form="♀ (female)"]
  J7 = female pin header, 17 pins [form="♀ (female)"]  # not connected
  J30 = female pin header, 17 pins [form="♀ (female)"]  # not connected
  J25 = female pin header, 19 pins [form="♀ (female)"]
  J31 = female pin header, 19 pins [form="♀ (female)"]
  J32 = female pin header, 19 pins [form="♀ (female)"]
  J23 = female pin header, 16 pins [form="♀ (female)"]  # not connected
  J16 = female pin header, 16 pins [form="♀ (female)"]  # not connected
  J33 = female pin header, 4 pins [form="♀ (female)"]
  J34 = female pin header, 6 pins [form="♀ (female)"]
  J11 = female pin header, 4 pins [form="♀ (female)"]

nets:
  N1: U1.RESET, S1.Pin_3, R1.Pin_0
  N2: U1.D0_(RX), J12.pin5
  N3: U1.D1_(TX), J12.pin4
  N4: U1.D2, J12.pin3
  N5: U1.D3_(PWM), J12.pin2
  N6: U1.D4, J12.pin1
  N7: U1.VCC, U1.AVCC, U1.AREF, R1.Pin_1, U2.output_voltage, C1.+, C5.1, J26.pin20, J27.pin20, J25.pin19, J31.pin19
  GND: U1.GND, S1.Pin_1, S1.Pin_2, U2.GND, C1.-, J1.pin1, C2.-, C3.2, C4.2, LED1.cathode, C5.0, J28.pin20, J29.pin20, J32.pin18, J32.pin19
  N8: U1.XLAT1, C3.1, XTAL1.pin_0
  N9: U1.XLAT2, C4.1, XTAL1.pin_1
  N10: U1.D5_(PWM), J11.pin4
  N11: U1.D6_(PWM), J11.pin3
  N12: U1.D7, J11.pin2
  N13: U1.D8, J11.pin1
  N14: U1.D9_(PWM), J33.pin1
  N15: U1.D10_(PWM), J33.pin2
  N16: U1.D11_(PWM), J33.pin3
  N17: U1.D12, J33.pin4
  N18: U1.D13, R2.Pin_0
  N19: U1.A0, J34.pin1
  N20: U1.A1, J34.pin2
  N21: U1.A2, J34.pin3
  N22: U1.A3, J34.pin4
  N23: U1.A4, J34.pin5
  N24: U1.A5, J34.pin6
  N25: U2.input_voltage, J1.pin2, C2.+
  N26: LED1.anode, R2.Pin_1

notes:
  v20210528-0001
  RESET
