# Fritzing sketch UnoPermanente (saved by Fritzing 0.9.6b)
circuit board: 6.3cm x 5.5cm
breadboards: 1

parts:
  U1 = Voltage Regulator - 5V [package="TO220 [THT]"]
  IC1 = MICROCONTROLLER [package=dil28-3-zif_socket]
  R1 = Resistor [tolerance=±5% power=0.25 resistance=10k package=THT]
  XTAL1 = Crystal [frequency="16 Mhz" package=THT]
  C3 = Ceramic Capacitor [capacitance=100nF voltage=35V package="100 mil [THT, multilayer]"]
  C7 = Electrolytic Capacitor [capacitance=10µF voltage=35V package="100 mil [THT, electrolytic]"]
  J2 = female pin header, 18 pins [form="♀ (female)"]  # not connected
  J3 = female pin header, 18 pins [form="♀ (female)"]  # not connected
  J4 = female pin header, 18 pins [form="♀ (female)"]  # not connected
  J5 = female pin header, 18 pins [form="♀ (female)"]  # not connected
  J6 = female pin header, 18 pins [form="♀ (female)"]  # not connected
  J7 = female pin header, 18 pins [form="♀ (female)"]  # not connected
  J8 = female pin header, 15 pins [form="♀ (female)"]  # not connected
  J9 = female pin header, 15 pins [form="♀ (female)"]  # not connected
  J10 = female pin header, 6 pins [form="♀ (female)"]  # not connected
  J12 = female pin header, 5 pins [form="♀ (female)"]  # not connected
  J14 = female pin header, 18 pins [form="♀ (female)"]  # not connected
  J15 = female pin header, 18 pins [form="♀ (female)"]  # not connected
  J16 = female pin header, 18 pins [form="♀ (female)"]  # not connected
  J18 = female pin header, 15 pins [form="♀ (female)"]  # not connected
  J19 = female pin header, 15 pins [form="♀ (female)"]  # not connected
  J20 = female pin header, 18 pins [form="♀ (female)"]  # not connected
  J21 = female pin header, 18 pins [form="♀ (female)"]  # not connected
  R2 = Resistor [tolerance=±5% power=0.25 resistance=220 package=THT]
  LED1 = LED - 5mm [color="Red (633nm)" current=0.030 package="5 mm [THT]"]
  C4 = Electrolytic Capacitor [capacitance=10µF voltage=35V package="100 mil [THT, electrolytic]"]
  S1 = Pushbutton [package="[THT]"]
  J1 = screw terminal, 2 pins
  C5 = Capacitor [package=cap-pth-5mm]
  C6 = Capacitor [package=cap-pth-5mm]

nets:
  N1: U1.input_voltage, C4.+, J1.pin2
  GND: U1.GND, IC1.GND, IC1.AGND, C3.1, C7.-, LED1.cathode, C4.-, S1.Pin_2, J1.pin1, C5.1, C6.1
  N2: U1.output_voltage, IC1.VCC, IC1.AVCC, IC1.AREF, R1.Pin_1, C3.0, C7.+
  N3: IC1.PC6(_RESET), R1.Pin_0, S1.Pin_3, S1.Pin_4
  N4: IC1.PB6(XTAL1_TOSC1), XTAL1.pin_1, C6.2
  N5: IC1.PB7(XTAL2_TOSC2), XTAL1.pin_0, C5.2
  N6: IC1.PB5(SCK), R2.Pin_0
  N7: R2.Pin_1, LED1.anode

notes:
  UnoPermanente
  v20210522
